// Logisim project lab5.circ as structural Verilog: 3 circuits, main circuit main_control_circuit
module main_control_circuit (
  input  I6,
  input  I5,
  input  I4,
  input  I3,
  input  I2,
  input  I1,
  input  I0,
  output MemtoReg,
  output RegWrite,
  output MemRead,
  output MemWrite,
  output Branch
);

  wire not_1_out, not_2_out;

  not not_1 (not_1_out, I6);
  not not_2 (not_2_out, I5);
  not not_3 (MemtoReg, I4);
  or or_1 (RegWrite, not_2_out, I4);
  and and_1 (MemRead, not_2_out, MemtoReg);
  and and_2 (MemWrite, not_1_out, I5, MemtoReg);

  assign Branch = I6;
endmodule

module instruction_memory (
  input  [25:0] Address,
  input  in_2,
  input  Clock,
  output [31:0] Instruction
);

  wire not_1_out;

  not not_1 (not_1_out, Clock);
  RAM #(.addrWidth(24), .dataWidth(32)) ram_1 (
    .addr(Address[25:2]), .we(in_2), .oe(not_1_out), .clk(not_1_out), .dout(Instruction));  // open: din
endmodule

module data_memory (
  input  [25:0] Address,
  input  MemWrite,
  input  MemRead,
  input  ClockIn,
  input  [31:0] WriteData,
  output [31:0] ReadData
);

  wire [31:0] RAM0_dout, RAM1_dout, RAM2_dout, RAM3_dout;

  RAM #(.addrWidth(24), .asyncread("true"), .dataWidth(32)) RAM0 (
    .addr(Address[23:0]), .we(MemWrite), .oe(MemRead), .clk(ClockIn), .din(WriteData), .dout(RAM0_dout));
  RAM #(.addrWidth(24), .asyncread("true"), .dataWidth(32)) RAM1 (
    .addr(Address[23:0]), .we(MemWrite), .oe(MemRead), .clk(ClockIn), .din(WriteData), .dout(RAM1_dout));
  RAM #(.addrWidth(24), .dataWidth(32)) RAM2 (
    .addr(Address[23:0]), .we(MemWrite), .oe(MemRead), .clk(ClockIn), .din(WriteData), .dout(RAM2_dout));
  RAM #(.addrWidth(24), .dataWidth(32)) RAM3 (
    .addr(Address[23:0]), .we(MemWrite), .oe(MemRead), .clk(ClockIn), .din(WriteData), .dout(RAM3_dout));
  Multiplexer #(.select(2), .width(32)) multiplexer_1 (
    .in0(RAM0_dout), .in1(RAM1_dout), .in2(RAM2_dout), .in3(RAM3_dout), .out(ReadData), .sel(Address[25:24]));
endmodule
